// Logisim project Relogio completo.circ as structural Verilog: 7 circuits, main circuit relogioDigital
module relogioDigital (
  input  in_1,
  input  up_down,
  output [3:0] out_3,
  output [3:0] out_4,
  output [3:0] out_5,
  output [3:0] out_6,
  output [3:0] out_7,
  output [3:0] out_8
);

  wire ACTIVE01, and_1_out, and_2_out, and_3_out, and_4_out, and_5_out, and_6_out, and_7_out, and_8_out,
       and_9_out, and_49_out, and_50_out, and_51_out, and_68_out, and_93_out, and_94_out, and_95_out,
       and_96_out, and_111_out, and_112_out, and_124_out, and_125_out, and_138_out, and_139_out, and_140_out,
       and_157_out, and_158_out, and_159_out, and_160_out, and_161_out, and_162_out, and_163_out,
       and_165_out, and_166_out, and_167_out, and_168_out, and_169_out, and_170_out, and_171_out,
       and_172_out, B2A, B10, BTN_EDGE, BTN_LATCH_RESET, BTN_PENDING, BTN_PENDING_BAR, BTN_PREV, C10, C12,
       circuito_display_en_1_a, circuito_display_en_1_b, circuito_display_en_1_c, circuito_display_en_1_d,
       circuito_display_en_1_e, circuito_display_en_1_f, circuito_display_en_1_g, circuito_display_en_2_a,
       circuito_display_en_2_b, circuito_display_en_2_c, circuito_display_en_2_d, circuito_display_en_2_e,
       circuito_display_en_2_f, circuito_display_en_2_g, circuito_display_en_3_a, circuito_display_en_3_b,
       circuito_display_en_3_c, circuito_display_en_3_d, circuito_display_en_3_e, circuito_display_en_3_f,
       circuito_display_en_3_g, circuito_display_en_4_a, circuito_display_en_4_b, circuito_display_en_4_c,
       circuito_display_en_4_d, circuito_display_en_4_e, circuito_display_en_4_f, circuito_display_en_4_g,
       circuito_display_en_5_a, circuito_display_en_5_b, circuito_display_en_5_c, circuito_display_en_5_d,
       circuito_display_en_5_e, circuito_display_en_5_f, circuito_display_en_5_g, circuito_display_en_6_a,
       circuito_display_en_6_b, circuito_display_en_6_c, circuito_display_en_6_d, circuito_display_en_6_e,
       circuito_display_en_6_f, circuito_display_en_6_g, CLK_MAIN, contador0a5_1_d0, contador0a5_1_d1,
       contador0a5_1_out_4, contador0a5_2_d0, contador0a5_2_d1, contador0a5_2_out_4, contador0a5_3_d0,
       contador0a5_3_d1, contador0a5_3_out_4, contador0a9_1_d0, contador0a9_1_d1, contador0a9_1_d3,
       contador0a9_1_out_6, contador0a9_2_d0, contador0a9_2_d1, contador0a9_2_d3, contador0a9_2_out_6,
       contador0a9_3_d0, contador0a9_3_d1, contador0a9_3_d3, contador0a9_3_out_6, contador5a0_d1,
       contador5a0_out_4, contador9a0_1_d1, contador9a0_1_d2, contador9a0_1_d3, contador9a0_2_d0,
       contador9a0_2_d1, contador9a0_2_d2, contador9a0_2_d3, D_BTN_PREV, d_ff_1_q, d_ff_3_q, d_ff_6_q,
       d_ff_13_q, d_ff_15_q, d_ff_16_q, D_TMR_C0, D_TMR_C1, D_TMR_C2, DEC0, DEC1, DEC2, DISPLAY_PREP, E_DOWN,
       E_UP, EN_ST, ENABLE_DISPLAY, HT0, HT1, HT2, LG_1, LG_2, LG_3, LG_4, LG_5, LG_6, LG_7, LG_8, LG_9,
       LG_10, LG_11, LG_12, LG_13, LG_14, LG_15, LG_16, LG_17, LG_18, LG_19, LG_20, LG_21, LG_22, LG_23,
       LG_24, LG_25, LG_26, LG_27, LG_28, LG_29, LG_30, LG_31, LG_32, LG_33, LG_34, LG_35, LG_36, LG_37,
       LG_38, LG_39, LG_40, LG_41, LG_42, LG_43, LG_44, LG_45, LG_46, LG_47, LG_48, LG_49, LG_50, LG_51,
       LG_52, LG_53, LG_54, LG_55, LG_56, LG_57, LG_58, LG_59, LG_60, LG_61, LG_62, LG_63, LG_64, LG_65,
       LG_66, LG_67, LG_68, LG_69, LG_70, LG_71, LG_72, LG_73, LG_74, LG_75, LG_76, LG_77, LG_78, LG_79,
       LG_80, LG_81, LG_82, LG_83, LG_84, LG_85, LG_86, LG_87, LG_88, LG_89, LG_90, LG_91, LG_92, LG_93,
       LG_94, LG_95, LG_96, LG_97, LG_98, LG_99, LG_100, LG_101, LG_102, LG_103, LG_104, LG_105, LG_106,
       LG_107, LG_108, LG_109, LG_110, LG_111, LG_112, LG_113, LG_114, LG_115, LG_116, LG_117, LG_118,
       LG_119, LG_120, LG_121, LG_122, LG_123, LG_124, LG_125, LG_126, LG_127, LG_128, LG_129, LG_130,
       LG_131, LG_132, LG_133, LG_134, LG_135, LG_136, LG_137, LG_138, LG_139, LG_140, LG_141, LG_142,
       LG_143, LG_144, LG_145, LG_146, LG_147, LG_148, LG_149, LG_150, LG_151, LG_152, LG_153, LG_154,
       LG_155, LG_156, LG_157, LG_158, LG_159, LG_160, LG_161, LG_162, LG_163, LG_164, LG_165, LG_166,
       LG_167, LG_168, LG_169, LG_170, LG_171, LG_172, LG_173, LG_174, LG_175, LG_176, LG_177, LG_178,
       LG_179, LG_180, LG_181, LG_182, LG_183, LG_184, LG_185, LG_186, LG_187, LG_188, MONO_ACTIVE,
       MONO_TRIGGER, MT0, MT1, MT2, nand_1_out, nand_2_out, nand_3_out, NAO_DOWN, nor_1_out, nor_2_out,
       NOR_C10, not_1_out, not_2_out, not_3_out, not_4_out, not_5_out, not_6_out, not_7_out, not_8_out,
       not_9_out, not_15_out, not_16_out, not_17_out, not_18_out, not_25_out, not_26_out, not_27_out,
       not_28_out, not_29_out, not_33_out, not_34_out, not_37_out, not_38_out, not_39_out, not_40_out,
       not_41_out, not_42_out, not_43_out, not_44_out, NOT_BTN_PREV, NOT_C0, NOT_C1, NOT_TRIGGER, or_29_out,
       or_30_out, or_41_out, or_44_out, or_45_out, or_47_out, or_48_out, or_49_out, or_50_out,
       relog_23_59_59_out, RESET_ALL, SEG_UN_0, SEG_UN_9, T_SEC, TMR_C0, TMR_C1, TMR_C2, xor_1_out,
       xor_2_out, xor_3_out, xor_4_out, xor_5_out, xor_6_out;
  wire [2:0] Q0_q;

  not not_1 (not_1_out, and_4_out);
  and and_1 (and_1_out, and_3_out, not_1_out);
  not not_2 (not_2_out, and_5_out);
  and and_2 (and_2_out, HT1, not_3_out);
  not not_3 (not_3_out, HT0);
  circuito_display_en circuito_display_en_1 (
    .D3(1'b0), .D2(HT2), .D1(HT1), .D0(HT0), .EN(ENABLE_DISPLAY), .a(circuito_display_en_1_a),
    .b(circuito_display_en_1_b), .c(circuito_display_en_1_c), .d(circuito_display_en_1_d),
    .e(circuito_display_en_1_e), .f(circuito_display_en_1_f), .g(circuito_display_en_1_g));
  D_Flip_Flop d_ff_1 (.clk(xor_2_out), .D(and_5_out), .Q(d_ff_1_q));  // open: Qn, preset, en, reset
  _7_Segment_Display u_7_segment_display_1 (
    .g(circuito_display_en_1_g), .f(circuito_display_en_1_f), .a(circuito_display_en_1_a),
    .b(circuito_display_en_1_b), .e(circuito_display_en_1_e), .d(circuito_display_en_1_d),
    .c(circuito_display_en_1_c));  // open: dp
  LED led_1 (.in(and_4_out));
  and and_3 (and_3_out, not_2_out, d_ff_1_q);
  D_Flip_Flop d_ff_2 (.clk(CLK_MAIN), .D(1'b0), .Q(HT2), .en(1'b1), .reset(RESET_ALL));  // open: Qn, preset
  and and_4 (and_4_out, and_8_out, and_2_out);
  not not_4 (not_4_out, HT1);
  D_Flip_Flop d_ff_3 (.clk(CLK_MAIN), .D(relog_23_59_59_out), .Q(d_ff_3_q));  // open: Qn, preset, en, reset
  LED led_2 (.in(relog_23_59_59_out));
  and and_5 (and_5_out, and_9_out, not_4_out);
  D_Flip_Flop d_ff_4 (.clk(CLK_MAIN), .D(LG_92), .Q(HT1), .en(1'b1), .reset(RESET_ALL));  // open: Qn, preset
  nand nand_1 (nand_1_out, HT0, HT1);
  and relog_23_59_59 (relog_23_59_59_out, and_49_out, and_4_out);
  not not_5 (not_5_out, out_4[2]);
  not not_6 (not_6_out, out_4[3]);
  not not_7 (not_7_out, out_4[1]);
  not not_8 (not_8_out, out_4[2]);
  D_Flip_Flop d_ff_5 (.clk(CLK_MAIN), .D(LG_117), .Q(HT0), .en(1'b1), .reset(RESET_ALL));  // open: Qn, preset
  not not_9 (not_9_out, nand_1_out);
  and and_6 (and_6_out, relog_23_59_59_out, d_ff_3_q);
  and and_7 (and_7_out, d_ff_3_q, CLK_MAIN);
  and and_8 (and_8_out, out_4[0], out_4[1], not_5_out, not_6_out);
  and and_9 (and_9_out, out_4[0], not_7_out, not_8_out, out_4[3]);
  contador0a5 contador0a5_1 (
    .Q2(HT2), .Q1(HT1), .Q0(HT0), .out_4(contador0a5_1_out_4), .D1(contador0a5_1_d1), .D0(contador0a5_1_d0));
  xor xor_1 (xor_1_out, not_9_out, and_6_out);
  not not_10 (LG_1, out_3[1]);
  and and_10 (LG_11, LG_1, LG_2);
  and and_11 (LG_21, LG_20, LG_3);
  or or_1 (LG_31, LG_24, LG_29);
  and and_12 (LG_41, MT1, LG_22);
  or or_2 (LG_51, LG_36, LG_50);
  and and_13 (LG_61, LG_60, LG_14);
  and and_14 (LG_71, LG_70, LG_3);
  and and_15 (LG_81, LG_69, LG_77);
  and and_16 (LG_91, LG_89, LG_90);
  and and_17 (LG_101, LG_100, LG_3);
  or or_3 (LG_111, LG_108, LG_109);
  and and_18 (LG_121, out_4[3], LG_66);
  or or_4 (LG_131, LG_120, LG_122);
  and and_19 (LG_141, LG_140, up_down);
  and and_20 (LG_151, LG_150, LG_3);
  and and_21 (LG_161, out_4[0], out_4[1]);
  and and_22 (LG_171, up_down, LG_75);
  and and_23 (LG_181, LG_14, LG_179);
  D_Flip_Flop d_ff_6 (.clk(xor_4_out), .D(and_51_out), .Q(d_ff_6_q));  // open: Qn, preset, en, reset
  circuito_display_en circuito_display_en_2 (
    .D3(out_4[3]), .D2(out_4[2]), .D1(out_4[1]), .D0(out_4[0]), .EN(ENABLE_DISPLAY),
    .a(circuito_display_en_2_a), .b(circuito_display_en_2_b), .c(circuito_display_en_2_c),
    .d(circuito_display_en_2_d), .e(circuito_display_en_2_e), .f(circuito_display_en_2_f),
    .g(circuito_display_en_2_g));
  _7_Segment_Display u_7_segment_display_2 (
    .g(circuito_display_en_2_g), .f(circuito_display_en_2_f), .a(circuito_display_en_2_a),
    .b(circuito_display_en_2_b), .e(circuito_display_en_2_e), .d(circuito_display_en_2_d),
    .c(circuito_display_en_2_c));  // open: dp
  D_Flip_Flop d_ff_7 (
    .clk(CLK_MAIN), .D(LG_138), .Q(out_4[3]), .Qn(out_8[3]), .en(1'b1), .reset(RESET_ALL));  // open: preset
  not not_11 (LG_2, out_3[2]);
  and and_24 (LG_12, LG_10, LG_11);
  not not_12 (LG_22, MT0);
  or or_5 (LG_32, LG_30, LG_31);
  and and_25 (LG_42, LG_41, LG_3);
  and and_26 (LG_52, T_SEC, LG_22);
  not not_13 (LG_62, LG_61);
  and and_27 (LG_72, HT0, out_4[0]);
  and and_28 (LG_82, LG_79, LG_80);
  or or_6 (LG_92, LG_63, LG_91);
  and and_29 (LG_102, HT1, up_down);
  or or_7 (LG_112, LG_110, LG_107);
  and and_30 (LG_122, LG_121, LG_3);
  or or_8 (LG_132, LG_125, LG_104);
  and and_31 (LG_142, out_4[1], out_4[2]);
  or or_9 (LG_152, LG_141, LG_143);
  and and_32 (LG_162, LG_161, up_down);
  and and_33 (LG_172, LG_76, LG_66);
  and and_34 (LG_182, LG_180, LG_181);
  xor xor_2 (xor_2_out, d_ff_6_q, and_51_out);
  D_Flip_Flop d_ff_8 (
    .clk(CLK_MAIN), .D(LG_159), .Q(out_4[2]), .Qn(out_8[2]), .en(1'b1), .reset(RESET_ALL));  // open: preset
  not not_14 (LG_3, up_down);
  and and_35 (LG_13, LG_12, LG_9);
  and and_36 (LG_23, MT2, LG_22);
  and and_37 (LG_33, T_SEC, LG_14);
  and and_38 (LG_43, MT0, LG_25);
  and and_39 (LG_53, LG_52, LG_14);
  and and_40 (LG_63, HT1, LG_62);
  and and_41 (LG_73, out_4[3], LG_3);
  and and_42 (LG_83, LG_81, LG_78);
  and and_43 (LG_93, HT0, LG_62);
  and and_44 (LG_103, LG_66, LG_69);
  or or_10 (LG_113, LG_111, LG_112);
  and and_45 (LG_123, out_4[0], out_4[1]);
  or or_11 (LG_133, LG_131, LG_132);
  and and_46 (LG_143, LG_142, LG_66);
  or or_12 (LG_153, LG_145, LG_147);
  and and_47 (LG_163, out_4[1], LG_66);
  and and_48 (LG_173, LG_171, LG_172);
  or or_13 (LG_183, LG_160, LG_182);
  not not_15 (not_15_out, 1'b0);
  not not_16 (not_16_out, 1'b0);
  D_Flip_Flop d_ff_9 (
    .clk(CLK_MAIN), .D(LG_183), .Q(out_4[1]), .Qn(out_8[1]), .en(1'b1), .reset(RESET_ALL));  // open: preset
  and and_49 (and_49_out, and_140_out, and_68_out);
  not not_17 (not_17_out, MT1);
  not not_18 (not_18_out, 1'b0);
  D_Flip_Flop d_ff_10 (
    .clk(CLK_MAIN), .D(LG_188), .Q(out_4[0]), .Qn(out_8[0]), .en(1'b1), .reset(RESET_ALL));  // open: preset
  and and_50 (and_50_out, not_17_out, not_18_out, MT2, MT0);
  and and_51 (and_51_out, not_15_out, MT1, MT2, not_16_out);
  contador0a9 contador0a9_1 (
    .Q3(out_4[3]), .Q2(out_4[2]), .Q1(out_4[1]), .Q0(out_4[0]), .D3(contador0a9_1_d3),
    .out_6(contador0a9_1_out_6), .D1(contador0a9_1_d1), .D0(contador0a9_1_d0));
  and and_52 (LG_4, out_3[0], out_3[3]);
  or or_14 (LG_14, LG_7, LG_13);
  and and_53 (LG_24, LG_23, LG_3);
  and and_54 (LG_34, LG_33, LG_32);
  and and_55 (LG_44, LG_26, LG_3);
  and and_56 (LG_54, MT0, LG_16);
  and and_57 (LG_64, HT1, out_4[0]);
  and and_58 (LG_74, LG_72, LG_73);
  and and_59 (LG_84, LG_82, LG_83);
  and and_60 (LG_94, HT0, out_4[1]);
  and and_61 (LG_104, LG_102, LG_103);
  and and_62 (LG_114, T_SEC, LG_59);
  and and_63 (LG_124, out_4[2], LG_3);
  or or_15 (LG_134, LG_133, LG_130);
  and and_64 (LG_144, out_4[3], up_down);
  or or_16 (LG_154, LG_152, LG_153);
  and and_65 (LG_164, LG_163, LG_3);
  and and_66 (LG_174, LG_173, LG_69);
  and and_67 (LG_184, T_SEC, LG_66);
  circuito_display_en circuito_display_en_3 (
    .D3(1'b0), .D2(MT2), .D1(MT1), .D0(MT0), .EN(ENABLE_DISPLAY), .a(circuito_display_en_3_a),
    .b(circuito_display_en_3_b), .c(circuito_display_en_3_c), .d(circuito_display_en_3_d),
    .e(circuito_display_en_3_e), .f(circuito_display_en_3_f), .g(circuito_display_en_3_g));
  D_Flip_Flop d_ff_11 (.clk(CLK_MAIN), .D(LG_35), .Q(MT2), .en(1'b1), .reset(RESET_ALL));  // open: Qn, preset
  and and_68 (and_68_out, and_50_out, and_94_out);
  _7_Segment_Display u_7_segment_display_3 (
    .g(circuito_display_en_3_g), .f(circuito_display_en_3_f), .a(circuito_display_en_3_a),
    .b(circuito_display_en_3_b), .e(circuito_display_en_3_e), .d(circuito_display_en_3_d),
    .c(circuito_display_en_3_c));  // open: dp
  and and_69 (LG_5, LG_1, LG_2);
  and and_70 (LG_15, T_SEC, LG_14);
  not not_19 (LG_25, MT1);
  or or_17 (LG_35, LG_17, LG_34);
  and and_71 (LG_45, LG_43, LG_44);
  or or_18 (LG_55, LG_53, LG_54);
  and and_72 (LG_65, LG_64, up_down);
  not not_20 (LG_75, HT0);
  or or_19 (LG_85, LG_65, LG_68);
  and and_73 (LG_95, HT0, out_4[2]);
  and and_74 (LG_105, out_4[0], out_4[3]);
  and and_75 (LG_115, LG_14, LG_113);
  and and_76 (LG_125, LG_123, LG_124);
  and and_77 (LG_135, T_SEC, LG_59);
  and and_78 (LG_145, LG_144, LG_66);
  or or_20 (LG_155, LG_154, LG_151);
  and and_79 (LG_165, out_4[2], up_down);
  or or_21 (LG_175, LG_162, LG_145);
  and and_80 (LG_185, LG_59, LG_14);
  D_Flip_Flop d_ff_12 (.clk(CLK_MAIN), .D(LG_51), .Q(MT1), .en(1'b1), .reset(RESET_ALL));  // open: Qn, preset
  D_Flip_Flop d_ff_13 (.clk(xor_4_out), .D(and_94_out), .Q(d_ff_13_q));  // open: Qn, preset, en, reset
  and and_81 (LG_6, LG_4, LG_5);
  not not_21 (LG_16, LG_15);
  not not_22 (LG_26, MT2);
  and and_82 (LG_36, MT1, LG_16);
  or or_22 (LG_46, LG_38, LG_40);
  and and_83 (LG_56, MT0, MT2);
  not not_23 (LG_66, out_4[0]);
  not not_24 (LG_76, HT1);
  or or_23 (LG_86, LG_71, LG_74);
  and and_84 (LG_96, HT0, out_4[0]);
  and and_85 (LG_106, LG_75, LG_3);
  and and_86 (LG_116, LG_114, LG_115);
  and and_87 (LG_126, HT0, up_down);
  and and_88 (LG_136, LG_14, LG_134);
  and and_89 (LG_146, out_4[2], LG_69);
  and and_90 (LG_156, T_SEC, LG_59);
  and and_91 (LG_166, LG_66, LG_69);
  or or_24 (LG_176, LG_164, LG_167);
  and and_92 (LG_186, LG_184, LG_185);
  not not_25 (not_25_out, and_94_out);
  not not_26 (not_26_out, out_3[1]);
  not not_27 (not_27_out, out_3[2]);
  not not_28 (not_28_out, nand_2_out);
  nand nand_2 (nand_2_out, MT2, MT1);
  and and_93 (and_93_out, d_ff_13_q, not_25_out);
  and and_94 (and_94_out, out_3[0], not_26_out, not_27_out, out_3[3]);
  contador0a5 contador0a5_2 (
    .Q2(MT2), .Q1(MT1), .Q0(MT0), .out_4(contador0a5_2_out_4), .D1(contador0a5_2_d1), .D0(contador0a5_2_d0));
  D_Flip_Flop d_ff_14 (.clk(CLK_MAIN), .D(LG_55), .Q(MT0), .en(1'b1), .reset(RESET_ALL));  // open: Qn, preset
  not not_29 (not_29_out, up_down);
  and and_95 (and_95_out, contador0a9_2_d1, not_29_out);
  and and_96 (and_96_out, contador9a0_1_d1, up_down);
  and and_97 (LG_7, LG_6, LG_3);
  and and_98 (LG_17, MT2, LG_16);
  and and_99 (LG_27, up_down, LG_22);
  and and_100 (LG_37, MT0, MT1);
  or or_25 (LG_47, LG_42, LG_45);
  and and_101 (LG_57, LG_25, LG_3);
  and and_102 (LG_67, HT1, out_4[1]);
  not not_30 (LG_77, out_4[2]);
  or or_26 (LG_87, LG_85, LG_86);
  and and_103 (LG_97, LG_96, up_down);
  and and_104 (LG_107, LG_105, LG_106);
  or or_27 (LG_117, LG_93, LG_116);
  and and_105 (LG_127, LG_66, LG_69);
  and and_106 (LG_137, LG_135, LG_136);
  and and_107 (LG_147, LG_146, LG_3);
  and and_108 (LG_157, LG_14, LG_155);
  and and_109 (LG_167, LG_165, LG_166);
  or or_28 (LG_177, LG_170, LG_174);
  and and_110 (LG_187, out_4[0], LG_62);
  D_Flip_Flop d_ff_15 (.clk(T_SEC), .D(and_139_out), .Q(d_ff_15_q));  // open: Qn, preset, en, reset
  xor xor_3 (xor_3_out, d_ff_15_q, and_139_out);
  D_Flip_Flop D3 (
    .clk(CLK_MAIN), .D(or_41_out), .Q(out_3[3]), .Qn(out_6[3]), .en(T_SEC), .reset(RESET_ALL));  // open: preset
  LED led_3 (.in(or_41_out));
  or or_29 (or_29_out, and_95_out, and_96_out);
  D_Flip_Flop D2 (
    .clk(CLK_MAIN), .D(or_30_out), .Q(out_3[2]), .Qn(out_6[2]), .en(T_SEC), .reset(RESET_ALL));  // open: preset
  LED led_4 (.in(or_30_out));
  xor xor_4 (xor_4_out, xor_3_out, up_down);
  circuito_display_en circuito_display_en_4 (
    .D3(out_3[3]), .D2(out_3[2]), .D1(out_3[1]), .D0(out_3[0]), .EN(ENABLE_DISPLAY),
    .a(circuito_display_en_4_a), .b(circuito_display_en_4_b), .c(circuito_display_en_4_c),
    .d(circuito_display_en_4_d), .e(circuito_display_en_4_e), .f(circuito_display_en_4_f),
    .g(circuito_display_en_4_g));
  LED led_5 (.in(or_29_out));
  and and_111 (and_111_out, contador0a9_2_out_6, not_29_out);
  or or_30 (or_30_out, and_111_out, and_112_out);
  and and_112 (and_112_out, contador9a0_1_d2, up_down);
  not not_31 (LG_8, out_3[0]);
  and and_113 (LG_18, MT0, MT2);
  and and_114 (LG_28, LG_25, LG_26);
  and and_115 (LG_38, LG_37, up_down);
  or or_31 (LG_48, LG_46, LG_47);
  and and_116 (LG_58, LG_56, LG_57);
  and and_117 (LG_68, LG_67, LG_66);
  not not_32 (LG_78, out_4[3]);
  or or_32 (LG_88, LG_87, LG_84);
  and and_118 (LG_98, HT0, out_4[3]);
  or or_33 (LG_108, LG_94, LG_95);
  and and_119 (LG_118, out_4[3], LG_62);
  and and_120 (LG_128, LG_77, LG_78);
  or or_34 (LG_138, LG_118, LG_137);
  and and_121 (LG_148, out_4[0], out_4[1]);
  and and_122 (LG_158, LG_156, LG_157);
  and and_123 (LG_168, out_4[0], LG_69);
  or or_35 (LG_178, LG_175, LG_176);
  or or_36 (LG_188, LG_186, LG_187);
  _7_Segment_Display u_7_segment_display_4 (
    .g(circuito_display_en_4_g), .f(circuito_display_en_4_f), .a(circuito_display_en_4_a),
    .b(circuito_display_en_4_b), .e(circuito_display_en_4_e), .d(circuito_display_en_4_d),
    .c(circuito_display_en_4_c));  // open: dp
  D_Flip_Flop D1 (
    .clk(CLK_MAIN), .D(or_29_out), .Q(out_3[1]), .Qn(out_6[1]), .en(T_SEC), .reset(RESET_ALL));  // open: preset
  not not_33 (not_33_out, 1'b0);
  not not_34 (not_34_out, Q0_q[1]);
  D_Flip_Flop D0 (
    .clk(CLK_MAIN), .D(contador0a9_2_d0), .Q(out_3[0]), .Qn(out_6[0]), .en(T_SEC), .reset(RESET_ALL));  // open: preset
  and and_124 (and_124_out, contador0a9_2_d3, not_29_out);
  and and_125 (and_125_out, contador9a0_1_d3, up_down);
  not not_35 (LG_9, out_3[3]);
  and and_126 (LG_19, LG_18, up_down);
  and and_127 (LG_29, LG_27, LG_28);
  and and_128 (LG_39, MT2, up_down);
  and and_129 (LG_49, T_SEC, LG_14);
  or or_37 (LG_59, LG_58, LG_29);
  not not_36 (LG_69, out_4[1]);
  and and_130 (LG_79, up_down, LG_75);
  and and_131 (LG_89, T_SEC, LG_59);
  and and_132 (LG_99, LG_98, LG_66);
  or or_38 (LG_109, LG_97, LG_99);
  and and_133 (LG_119, out_4[0], out_4[3]);
  and and_134 (LG_129, LG_126, LG_127);
  and and_135 (LG_139, out_4[2], LG_62);
  and and_136 (LG_149, LG_76, LG_77);
  or or_39 (LG_159, LG_139, LG_158);
  and and_137 (LG_169, LG_78, LG_3);
  or or_40 (LG_179, LG_178, LG_177);
  and and_138 (and_138_out, not_33_out, Q0_q[0], not_34_out, Q0_q[2]);
  not not_37 (not_37_out, 1'b0);
  contador9a0 contador9a0_1 (
    .Q3(out_3[3]), .Q2(out_3[2]), .Q1(out_3[1]), .Q0(out_3[0]), .D3(contador9a0_1_d3), .D2(contador9a0_1_d2),
    .D1(contador9a0_1_d1));  // open: D0
  LED led_6 (.in(and_124_out));
  or or_41 (or_41_out, and_124_out, and_125_out);
  LED led_7 (.in(and_125_out));
  not not_38 (not_38_out, Q0_q[0]);
  and and_139 (and_139_out, Q0_q[1], not_38_out, Q0_q[2], not_37_out);
  contador0a9 contador0a9_2 (
    .Q3(out_3[3]), .Q2(out_3[2]), .Q1(out_3[1]), .Q0(out_3[0]), .D3(contador0a9_2_d3),
    .out_6(contador0a9_2_out_6), .D1(contador0a9_2_d1), .D0(contador0a9_2_d0));
  LED led_8 (.in(contador9a0_1_d3));
  LED led_9 (.in(or_41_out));
  and and_140 (and_140_out, SEG_UN_9, and_138_out);
  and and_141 (LG_10, up_down, LG_8);
  and and_142 (LG_20, MT0, MT1);
  or or_42 (LG_30, LG_19, LG_21);
  and and_143 (LG_40, LG_39, LG_22);
  and and_144 (LG_50, LG_49, LG_48);
  and and_145 (LG_60, T_SEC, LG_59);
  and and_146 (LG_70, HT1, LG_69);
  and and_147 (LG_80, LG_76, LG_66);
  and and_148 (LG_90, LG_14, LG_88);
  and and_149 (LG_100, HT0, LG_78);
  or or_43 (LG_110, LG_101, LG_104);
  and and_150 (LG_120, LG_119, up_down);
  and and_151 (LG_130, LG_129, LG_128);
  and and_152 (LG_140, out_4[0], out_4[2]);
  and and_153 (LG_150, LG_148, LG_149);
  and and_154 (LG_160, out_4[1], LG_62);
  and and_155 (LG_170, LG_168, LG_169);
  and and_156 (LG_180, T_SEC, LG_59);
  not not_39 (not_39_out, up_down);
  LED led_10 (.in(and_140_out));
  D_Flip_Flop Q2 (.clk(CLK_MAIN), .D(or_44_out), .Q(Q0_q[2]), .en(EN_ST), .reset(RESET_ALL));  // open: Qn, preset
  contador5a0 contador5a0 (
    .Q2(Q0_q[2]), .Q1(Q0_q[1]), .Q0(Q0_q[0]), .out_4(contador5a0_out_4), .D1(contador5a0_d1));  // open: D0
  circuito_display_en circuito_display_en_5 (
    .D3(1'b0), .D2(Q0_q[2]), .D1(Q0_q[1]), .D0(Q0_q[0]), .EN(ENABLE_DISPLAY), .a(circuito_display_en_5_a),
    .b(circuito_display_en_5_b), .c(circuito_display_en_5_c), .d(circuito_display_en_5_d),
    .e(circuito_display_en_5_e), .f(circuito_display_en_5_f), .g(circuito_display_en_5_g));
  not not_40 (not_40_out, up_down);
  and and_157 (and_157_out, and_140_out, not_39_out);
  and and_158 (and_158_out, and_163_out, up_down);
  nor nor_1 (nor_1_out, Q0_q[2], Q0_q[1], Q0_q[0]);
  _7_Segment_Display u_7_segment_display_5 (
    .g(circuito_display_en_5_g), .f(circuito_display_en_5_f), .a(circuito_display_en_5_a),
    .b(circuito_display_en_5_b), .e(circuito_display_en_5_e), .d(circuito_display_en_5_d),
    .c(circuito_display_en_5_c));  // open: dp
  and and_159 (and_159_out, contador0a5_3_out_4, not_40_out);
  and and_160 (and_160_out, contador5a0_out_4, up_down);
  and and_161 (and_161_out, contador0a5_3_d1, not_40_out);
  and and_162 (and_162_out, contador5a0_d1, up_down);
  D_Flip_Flop Q1 (.clk(CLK_MAIN), .D(or_45_out), .Q(Q0_q[1]), .en(EN_ST), .reset(RESET_ALL));  // open: Qn, preset
  nand nand_3 (nand_3_out, Q0_q[2], Q0_q[1]);
  or or_44 (or_44_out, and_159_out, and_160_out);
  or or_45 (or_45_out, and_161_out, and_162_out);
  or or_46 (T_SEC, and_157_out, and_158_out);
  D_Flip_Flop Q0 (
    .clk(CLK_MAIN), .D(contador0a5_3_d0), .Q(Q0_q[0]), .en(EN_ST), .reset(RESET_ALL));  // open: Qn, preset
  not not_41 (not_41_out, nand_3_out);
  LED led_11 (.in(or_45_out));
  LED led_12 (.in(T_SEC));
  and and_163 (and_163_out, nor_1_out, SEG_UN_0);
  contador0a5 contador0a5_3 (
    .Q2(Q0_q[2]), .Q1(Q0_q[1]), .Q0(Q0_q[0]), .out_4(contador0a5_3_out_4), .D1(contador0a5_3_d1),
    .D0(contador0a5_3_d0));
  LED led_13 (.in(and_163_out));
  LED led_14 (.in(nor_2_out));
  LED led_15 (.in(Q0_q[0]));
  nor nor_2 (nor_2_out, SEG_UN_9, out_5[3], out_5[1], out_5[0]);
  D_Flip_Flop d_ff_16 (.clk(SEG_UN_9), .D(SEG_UN_9), .Q(d_ff_16_q));  // open: Qn, preset, en, reset
  Clock clock_1 (.out(CLK_MAIN));
  D_Flip_Flop D3_2 (.clk(CLK_MAIN), .D(or_47_out), .Q(out_5[3]), .Qn(out_7[3]), .reset(RESET_ALL));  // open: preset, en
  LED led_16 (.in(xor_6_out));
  xor xor_5 (xor_5_out, d_ff_16_q, SEG_UN_9);
  LED led_17 (.in(out_7[3]));
  D_Flip_Flop D2_2 (.clk(CLK_MAIN), .D(or_48_out), .Q(out_5[2]), .Qn(out_7[2]), .reset(RESET_ALL));  // open: preset, en
  xor xor_6 (xor_6_out, xor_5_out, up_down);
  LED led_18 (.in(or_49_out));
  D_Flip_Flop D1_2 (.clk(CLK_MAIN), .D(or_49_out), .Q(out_5[1]), .Qn(out_7[1]), .reset(RESET_ALL));  // open: preset, en
  D_Flip_Flop D0_2 (
    .clk(CLK_MAIN), .D(contador0a9_3_d0), .Q(out_5[0]), .Qn(out_7[0]), .reset(RESET_ALL));  // open: preset, en
  nor nor_3 (SEG_UN_0, out_5[0], out_5[2], out_5[1], out_5[3]);
  not not_42 (not_42_out, out_5[2]);
  not not_43 (not_43_out, out_5[1]);
  LED led_19 (.in(contador0a9_3_out_6));
  and and_164 (SEG_UN_9, out_5[0], not_42_out, not_43_out, out_5[3]);
  circuito_display_en circuito_display_en_6 (
    .D3(out_5[3]), .D2(out_5[2]), .D1(out_5[1]), .D0(out_5[0]), .EN(ENABLE_DISPLAY),
    .a(circuito_display_en_6_a), .b(circuito_display_en_6_b), .c(circuito_display_en_6_c),
    .d(circuito_display_en_6_d), .e(circuito_display_en_6_e), .f(circuito_display_en_6_f),
    .g(circuito_display_en_6_g));
  contador9a0 contador9a0_2 (
    .Q3(out_5[3]), .Q2(out_5[2]), .Q1(out_5[1]), .Q0(out_5[0]), .D3(contador9a0_2_d3), .D2(contador9a0_2_d2),
    .D1(contador9a0_2_d1), .D0(contador9a0_2_d0));
  contador0a9 contador0a9_3 (
    .Q3(out_5[3]), .Q2(out_5[2]), .Q1(out_5[1]), .Q0(out_5[0]), .D3(contador0a9_3_d3),
    .out_6(contador0a9_3_out_6), .D1(contador0a9_3_d1), .D0(contador0a9_3_d0));
  _7_Segment_Display u_7_segment_display_6 (
    .g(circuito_display_en_6_g), .f(circuito_display_en_6_f), .a(circuito_display_en_6_a),
    .b(circuito_display_en_6_b), .e(circuito_display_en_6_e), .d(circuito_display_en_6_d),
    .c(circuito_display_en_6_c));  // open: dp
  not not_44 (not_44_out, up_down);
  LED led_20 (.in(and_165_out));
  and and_165 (and_165_out, contador0a9_3_d3, not_44_out);
  and and_166 (and_166_out, contador9a0_2_d3, up_down);
  and and_167 (and_167_out, contador0a9_3_out_6, not_44_out);
  and and_168 (and_168_out, contador9a0_2_d2, up_down);
  LED led_21 (.in(and_169_out));
  and and_169 (and_169_out, not_44_out, contador0a9_3_d1);
  and and_170 (and_170_out, up_down, contador9a0_2_d1);
  LED led_22 (.in(and_170_out));
  and and_171 (and_171_out, not_44_out, contador0a9_3_d0);
  and and_172 (and_172_out, up_down, contador9a0_2_d0);
  or or_47 (or_47_out, and_165_out, and_166_out);
  LED led_23 (.in(and_166_out));
  LED led_24 (.in(and_167_out));
  or or_48 (or_48_out, and_167_out, and_168_out);
  LED led_25 (.in(and_168_out));
  or or_49 (or_49_out, and_169_out, and_170_out);
  or or_50 (or_50_out, and_171_out, and_172_out);
  LED led_26 (.in(or_47_out));
  LED led_27 (.in(or_48_out));
  LED led_28 (.in(or_49_out));
  LED led_29 (.in(or_50_out));
  Button MOSTRAR_HORA (.out(D_BTN_PREV));
  Button RESET (.out(RESET_ALL));
  not not_45 (NAO_DOWN, up_down);
  // AND_Gate and_173 has open pins: out=E_UP
  // AND_Gate and_174 has open pins: out=E_DOWN
  LED DISPLAY_ATIVO (.in(ENABLE_DISPLAY));
  LED MINUTO___TRIGGER (.in(T_SEC));
  // OR_Gate or_51 has open pins: out=EN_ST
  not not_46 (NOT_BTN_PREV, BTN_PREV);
  not not_47 (NOT_C0, TMR_C0);
  not not_48 (NOT_C1, TMR_C1);
  or or_52 (C12, TMR_C1, TMR_C2);
  and and_175 (B10, TMR_C1, TMR_C0);
  or or_53 (C10, TMR_C1, TMR_C0);
  and and_176 (BTN_EDGE, D_BTN_PREV, NOT_BTN_PREV);
  not not_49 (NOT_TRIGGER, MONO_TRIGGER);
  or or_54 (MONO_TRIGGER, BTN_PENDING, T_SEC);
  and and_177 (DEC0, NOT_C0, C12);
  and and_178 (NOR_C10, NOT_C1, NOT_C0);
  and and_179 (DEC2, TMR_C2, C10);
  D_Flip_Flop d_ff_17 (.clk(CLK_MAIN), .D(D_BTN_PREV), .Q(BTN_PREV), .en(1'b1), .reset(RESET_ALL));  // open: Qn, preset
  D_Flip_Flop d_ff_18 (.clk(CLK_MAIN), .D(D_TMR_C0), .Q(TMR_C0), .en(1'b1), .reset(RESET_ALL));  // open: Qn, preset
  or or_55 (D_TMR_C0, MONO_TRIGGER, DEC0);
  and and_180 (B2A, TMR_C2, NOR_C10);
  or or_56 (D_TMR_C2, MONO_TRIGGER, DEC2);
  or or_57 (ACTIVE01, TMR_C0, TMR_C1);
  D_Flip_Flop d_ff_19 (.clk(CLK_MAIN), .D(D_TMR_C1), .Q(TMR_C1), .en(1'b1), .reset(RESET_ALL));  // open: Qn, preset
  or or_58 (MONO_ACTIVE, ACTIVE01, TMR_C2);
  or or_59 (DEC1, B10, B2A);
  D_Flip_Flop d_ff_20 (.clk(CLK_MAIN), .D(D_TMR_C2), .Q(TMR_C2), .en(1'b1), .reset(RESET_ALL));  // open: Qn, preset
  and and_181 (D_TMR_C1, NOT_TRIGGER, DEC1);
  or or_60 (DISPLAY_PREP, MONO_ACTIVE, BTN_PENDING);
  or or_61 (BTN_LATCH_RESET, MONO_ACTIVE, RESET_ALL);
  or or_62 (ENABLE_DISPLAY, DISPLAY_PREP, D_BTN_PREV);
  // NOR_Gate nor_4 has open pins: out=BTN_PENDING
  // NOR_Gate nor_5 has open pins: out=BTN_PENDING_BAR

  // Other names for the same wires on the sheet: MOSTRAR_HORA = D_BTN_PREV; NX_HT0 = LG_117; NX_HT1 = LG_92;
  //   NX_HU0 = LG_188; NX_HU1 = LG_183; NX_HU2 = LG_159; NX_HU3 = LG_138; NX_MT0 = LG_55; NX_MT1 = LG_51;
  //   NX_MT2 = LG_35; MU0 = out_3[0]; MU1 = out_3[1]; MU2 = out_3[2]; MU3 = out_3[3]; HU0 = out_4[0]; HU1 = out_4[1];
  //   HU2 = out_4[2]; HU3 = out_4[3]; TRIG_MINUTO = T_SEC; DIRECAO_UPDOWN = up_down; U_DIR = up_down

  // Notes on the sheet:
  //   Contador de 0 a 2, para horas
  //   dezena = 2
  //   identifica o 09 e 19
  //   Contador de 0 a 9, para unidade de minutos e segundos
  //   hora = 23
  //   identifica o 23 na hora
  //   unidade = 3
  //   identifica o 9
  //   SEL (UP/DOWN): [UP AND (NOT DIR)] OR [DOWN AND DIR]
  //   UP / DOWN - DEZENAS MINUTOS E HORAS (CLOCK SINCRONO)
  //   T_SEC: virada de segundos 59/00 | CLK_MAIN: clock dos segundos | U_DIR: direcao
  //   Minuto dezena 0..5; Hora 00..23; sinais NX alimentam os flip-flops existentes
  //   Contador de 0 a 5, para dezenas de minutos e segundos
  //   identifica o 5  na dezena de minutos
  //   identifica o 9 na unidade de minutos
  //   identifica o 5 na dezena do seg
  //   identifica o 0 na dezena do seg
  //   identifica 0 9 na unidade de segundos
  //   identificando 0 na unidade de segudndos
  //   CARRY/BORROW DA DEZENA DOS SEGUNDOS
  //   MUX = AND/OR/NOT (sem multiplexer pronto)
  //   Sem Multiplexer pronto; selecao e memoria do botao por portas
  //   MONOESTAVEL DIGITAL 5s - FF + AND / OR / NOT
  //   TRIG = virada do minuto OU clique guardado em latch NOR
  //   ENABLE_DISPLAY liga os seis decodificadores em paralelo
  //   RESET limpa os FF do relogio, do botao e do temporizador
  //   C=101 -> 100 -> 011 -> 010 -> 001 -> 000 (1 Hz)
endmodule

module contador0a9 (
  input  Q3,
  input  Q2,
  input  Q1,
  input  Q0,
  output D3,
  output out_6,
  output D1,
  output D0
);

  wire and_1_out, and_2_out, and_3_out, and_4_out, and_5_out, and_6_out, and_7_out, not_1_out, not_2_out,
       not_3_out, not_4_out, not_5_out, not_6_out, not_7_out, not_8_out;

  not not_1 (not_1_out, Q1);
  not not_2 (not_2_out, Q0);
  not not_3 (not_3_out, Q0);
  not not_4 (not_4_out, Q2);
  not not_5 (not_5_out, Q1);
  not not_6 (not_6_out, Q1);
  not not_7 (not_7_out, Q3);
  not not_8 (not_8_out, Q0);
  and and_1 (and_1_out, Q2, Q1, Q0);
  and and_2 (and_2_out, not_1_out, Q3, not_2_out);
  and and_3 (and_3_out, Q2, Q1, not_3_out);
  and and_4 (and_4_out, Q0, Q1, not_4_out);
  and and_5 (and_5_out, Q2, not_5_out);
  and and_6 (and_6_out, not_6_out, Q0, not_7_out);
  and and_7 (and_7_out, Q1, not_8_out);
  or or_1 (D3, and_1_out, and_2_out);
  or or_2 (out_6, and_3_out, and_4_out, and_5_out);
  or or_3 (D1, and_6_out, and_7_out);
  not not_9 (D0, Q0);

  // Notes on the sheet:
  //   CONTADOR DE 0 A 9
endmodule

module contador0a5 (
  input  Q2,
  input  Q1,
  input  Q0,
  output out_4,
  output D1,
  output D0
);

  wire and_1_out, and_2_out, and_3_out, and_4_out, and_5_out, not_1_out, not_2_out, not_3_out, not_4_out,
       not_5_out;

  not not_1 (not_1_out, Q0);
  not not_2 (not_2_out, Q2);
  not not_3 (not_3_out, Q1);
  not not_4 (not_4_out, Q1);
  not not_5 (not_5_out, Q0);
  and and_1 (and_1_out, Q2, Q1, not_1_out);
  and and_2 (and_2_out, Q0, Q1, not_2_out);
  and and_3 (and_3_out, Q2, not_3_out);
  and and_4 (and_4_out, not_4_out, Q0);
  and and_5 (and_5_out, Q1, not_5_out);
  or or_1 (out_4, and_1_out, and_2_out, and_3_out);
  or or_2 (D1, and_4_out, and_5_out);
  not not_6 (D0, Q0);
endmodule

module circuito_display (
  input  D3,
  input  D2,
  input  D1,
  input  D0,
  output a,
  output b,
  output c,
  output d,
  output e,
  output f,
  output g
);

  wire nand_1_out, nand_2_out, nand_3_out, nand_4_out, nand_5_out, nand_6_out, nand_7_out, nand_8_out,
       nand_9_out, nand_10_out, nand_11_out, nand_12_out, nand_13_out, nand_14_out, nand_15_out, nand_16_out,
       nand_17_out, nand_18_out, nand_19_out, nand_20_out, nand_21_out, nand_22_out, nand_23_out,
       nand_24_out, nand_25_out, nand_26_out, nand_27_out, nand_28_out, nand_29_out, nand_30_out,
       nand_31_out, nand_32_out, nand_33_out, nand_34_out, nand_35_out, nand_36_out, nand_37_out,
       nand_38_out, nand_39_out, nand_40_out, nand_41_out, nand_42_out, nand_43_out, nand_44_out,
       nand_45_out, nand_46_out, nand_47_out, nand_48_out, nand_49_out, nand_50_out, nand_51_out,
       nand_52_out, nand_53_out, nand_54_out, nand_55_out, nand_56_out, nand_57_out, nand_58_out,
       nand_59_out, nand_60_out, nand_61_out, nand_62_out, nand_63_out, nand_64_out, nand_65_out,
       nand_66_out, nand_67_out, nand_68_out, nand_69_out, nand_70_out, nand_71_out, nand_72_out,
       nand_73_out, nand_74_out, nand_75_out, nand_76_out, nand_77_out, nand_78_out, nand_79_out,
       nand_80_out, nand_81_out, nand_83_out, nand_84_out, nand_85_out, nand_86_out, nand_87_out,
       nand_88_out, nand_89_out, nand_90_out, nand_91_out, nand_92_out, nand_93_out, nand_94_out,
       nand_95_out, nand_96_out, nand_97_out, nand_98_out, nand_99_out, nand_100_out, nand_101_out,
       nand_102_out, nand_103_out, nand_104_out, nand_105_out, nand_106_out, nand_107_out, nand_108_out,
       nand_109_out, nand_110_out, nand_111_out, nand_112_out, nand_113_out, nand_114_out, nand_115_out,
       nand_116_out, nand_117_out, nand_118_out, nand_119_out, nand_120_out, nand_121_out, nand_122_out,
       nand_123_out, nand_124_out, nand_125_out, nand_126_out, nand_127_out, nand_128_out, nand_129_out,
       nand_130_out, nand_131_out, nand_132_out, nand_133_out, nand_134_out, nand_135_out, nand_136_out,
       nand_137_out, nand_138_out, nand_139_out, nand_141_out, nand_142_out, nand_143_out, nand_144_out,
       nand_146_out, nand_147_out, nand_148_out;

  nand nand_1 (nand_1_out, D2, D2);
  nand nand_2 (nand_2_out, D3, D3);
  nand nand_3 (nand_3_out, D1, D1);
  nand nand_4 (nand_4_out, D3, D3);
  nand nand_5 (nand_5_out, D1, D1);
  nand nand_6 (nand_6_out, D3, D3);
  nand nand_7 (nand_7_out, D3, D3);
  nand nand_8 (nand_8_out, D2, D2);
  nand nand_9 (nand_9_out, D2, D2);
  nand nand_10 (nand_10_out, D2, D2);
  nand nand_11 (nand_11_out, D0, D0);
  nand nand_12 (nand_12_out, D0, D0);
  nand nand_13 (nand_13_out, D3, D3);
  nand nand_14 (nand_14_out, D2, D2);
  nand nand_15 (nand_15_out, D0, D0);
  nand nand_16 (nand_16_out, D3, D3);
  nand nand_17 (nand_17_out, D2, D2);
  nand nand_18 (nand_18_out, D0, D0);
  nand nand_19 (nand_19_out, D3, D3);
  nand nand_20 (nand_20_out, D3, D3);
  nand nand_21 (nand_21_out, D3, nand_1_out);
  nand nand_22 (nand_22_out, D3, D3);
  nand nand_23 (nand_23_out, D2, D2);
  nand nand_24 (nand_24_out, nand_2_out, nand_3_out);
  nand nand_25 (nand_25_out, nand_4_out, nand_5_out);
  nand nand_26 (nand_26_out, nand_6_out, D0);
  nand nand_27 (nand_27_out, nand_7_out, nand_8_out);
  nand nand_28 (nand_28_out, nand_9_out, D1);
  nand nand_29 (nand_29_out, nand_10_out, nand_11_out);
  nand nand_30 (nand_30_out, D1, nand_12_out);
  nand nand_31 (nand_31_out, D3, D1);
  nand nand_32 (nand_32_out, D3, D2);
  nand nand_33 (nand_33_out, D1, D1);
  nand nand_34 (nand_34_out, D0, D0);
  nand nand_35 (nand_35_out, nand_13_out, D2);
  nand nand_36 (nand_36_out, nand_14_out, D1);
  nand nand_37 (nand_37_out, D1, nand_15_out);
  nand nand_38 (nand_38_out, nand_16_out, D2);
  nand nand_39 (nand_39_out, nand_17_out, nand_18_out);
  nand nand_40 (nand_40_out, nand_19_out, D1);
  nand nand_41 (nand_41_out, nand_20_out, D2);
  nand nand_42 (nand_42_out, nand_21_out, nand_21_out);
  nand nand_43 (nand_43_out, D1, D1);
  nand nand_44 (nand_44_out, nand_22_out, nand_23_out);
  nand nand_45 (nand_45_out, nand_24_out, nand_24_out);
  nand nand_46 (nand_46_out, D0, D0);
  nand nand_47 (nand_47_out, D3, D3);
  nand nand_48 (nand_48_out, D1, D1);
  nand nand_49 (nand_49_out, nand_25_out, nand_26_out);
  nand nand_50 (nand_50_out, nand_27_out, nand_27_out);
  nand nand_51 (nand_51_out, D0, D0);
  nand nand_52 (nand_52_out, nand_28_out, nand_28_out);
  nand nand_53 (nand_53_out, D1, D1);
  nand nand_54 (nand_54_out, D1, D1);
  nand nand_55 (nand_55_out, nand_29_out, nand_30_out);
  nand nand_56 (nand_56_out, nand_31_out, nand_32_out);
  nand nand_57 (nand_57_out, nand_33_out, nand_34_out);
  nand nand_58 (nand_58_out, nand_35_out, nand_35_out);
  nand nand_59 (nand_59_out, D1, D1);
  nand nand_60 (nand_60_out, nand_36_out, nand_37_out);
  nand nand_61 (nand_61_out, nand_38_out, nand_38_out);
  nand nand_62 (nand_62_out, D1, D1);
  nand nand_63 (nand_63_out, D2, D2);
  nand nand_64 (nand_64_out, nand_39_out, nand_40_out);
  nand nand_65 (nand_65_out, D2, D1);
  nand nand_66 (nand_66_out, nand_42_out, nand_43_out);
  nand nand_67 (nand_67_out, nand_45_out, nand_46_out);
  nand nand_68 (nand_68_out, D2, D2);
  nand nand_69 (nand_69_out, D0, D0);
  nand nand_70 (nand_70_out, nand_47_out, D1);
  nand nand_71 (nand_71_out, D3, nand_48_out);
  nand nand_72 (nand_72_out, nand_49_out, nand_49_out);
  nand nand_73 (nand_73_out, D1, D1);
  nand nand_74 (nand_74_out, D3, D3);
  nand nand_75 (nand_75_out, D2, D2);
  nand nand_76 (nand_76_out, nand_50_out, nand_51_out);
  nand nand_77 (nand_77_out, nand_52_out, D0);
  nand nand_78 (nand_78_out, D2, nand_53_out);
  nand nand_79 (nand_79_out, D2, D1);
  nand nand_80 (nand_80_out, D3, nand_54_out);
  nand nand_81 (nand_81_out, nand_55_out, nand_55_out);
  nand nand_82 (e, nand_81_out, nand_83_out);
  nand nand_83 (nand_83_out, nand_56_out, nand_56_out);
  nand nand_84 (nand_84_out, nand_58_out, nand_59_out);
  nand nand_85 (nand_85_out, nand_60_out, nand_60_out);
  nand nand_86 (nand_86_out, nand_61_out, nand_62_out);
  nand nand_87 (nand_87_out, D3, nand_63_out);
  nand nand_88 (nand_88_out, D3, D0);
  nand nand_89 (nand_89_out, nand_64_out, nand_64_out);
  nand nand_90 (nand_90_out, nand_41_out, nand_41_out);
  nand nand_91 (nand_91_out, nand_65_out, nand_66_out);
  nand nand_92 (nand_92_out, D0, D0);
  nand nand_93 (nand_93_out, nand_44_out, nand_67_out);
  nand nand_94 (nand_94_out, nand_68_out, nand_69_out);
  nand nand_95 (nand_95_out, nand_70_out, nand_70_out);
  nand nand_96 (nand_96_out, nand_71_out, nand_71_out);
  nand nand_97 (nand_97_out, nand_73_out, D0);
  nand nand_98 (nand_98_out, nand_99_out, nand_100_out);
  nand nand_99 (nand_99_out, nand_74_out, D2);
  nand nand_100 (nand_100_out, D3, nand_75_out);
  nand nand_101 (nand_101_out, nand_76_out, nand_77_out);
  nand nand_102 (nand_102_out, nand_78_out, nand_78_out);
  nand nand_103 (nand_103_out, nand_79_out, nand_79_out);
  nand nand_104 (nand_104_out, D0, D0);
  nand nand_105 (nand_105_out, nand_80_out, nand_80_out);
  nand nand_106 (nand_106_out, D0, D0);
  nand nand_107 (nand_107_out, nand_57_out, nand_84_out);
  nand nand_108 (nand_108_out, D0, D0);
  nand nand_109 (nand_109_out, D2, D2);
  nand nand_110 (nand_110_out, nand_85_out, nand_86_out);
  nand nand_111 (nand_111_out, nand_87_out, nand_88_out);
  nand nand_112 (nand_112_out, nand_90_out, D0);
  nand nand_113 (nand_113_out, nand_91_out, nand_91_out);
  nand nand_114 (nand_114_out, D3, nand_92_out);
  nand nand_115 (nand_115_out, nand_93_out, nand_93_out);
  nand nand_116 (nand_116_out, nand_95_out, D0);
  nand nand_117 (nand_117_out, nand_96_out, D0);
  nand nand_118 (nand_118_out, nand_72_out, nand_97_out);
  nand nand_119 (nand_119_out, nand_98_out, nand_98_out);
  nand nand_120 (nand_120_out, nand_101_out, nand_101_out);
  nand nand_121 (nand_121_out, nand_102_out, D0);
  nand nand_122 (nand_122_out, nand_103_out, nand_104_out);
  nand nand_123 (nand_123_out, nand_105_out, nand_106_out);
  nand nand_124 (nand_124_out, nand_107_out, nand_107_out);
  nand nand_125 (nand_125_out, nand_124_out, nand_126_out);
  nand nand_126 (nand_126_out, D2, nand_108_out);
  nand nand_127 (nand_127_out, D3, nand_109_out);
  nand nand_128 (nand_128_out, D3, D1);
  nand nand_129 (nand_129_out, nand_110_out, nand_110_out);
  nand nand_130 (nand_130_out, nand_111_out, nand_111_out);
  nand nand_131 (nand_131_out, nand_89_out, nand_112_out);
  nand nand_132 (nand_132_out, nand_113_out, nand_114_out);
  nand nand_133 (nand_133_out, nand_115_out, nand_94_out);
  nand nand_134 (nand_134_out, nand_116_out, nand_117_out);
  nand nand_135 (nand_135_out, nand_118_out, nand_118_out);
  nand nand_136 (nand_136_out, nand_120_out, nand_121_out);
  nand nand_137 (nand_137_out, nand_122_out, nand_123_out);
  nand nand_138 (nand_138_out, nand_125_out, nand_125_out);
  nand nand_139 (nand_139_out, nand_127_out, nand_128_out);
  nand nand_140 (g, nand_129_out, nand_130_out);
  nand nand_141 (nand_141_out, nand_131_out, nand_131_out);
  nand nand_142 (nand_142_out, nand_132_out, nand_132_out);
  nand nand_143 (nand_143_out, nand_133_out, nand_133_out);
  nand nand_144 (nand_144_out, nand_134_out, nand_134_out);
  nand nand_145 (c, nand_135_out, nand_119_out);
  nand nand_146 (nand_146_out, nand_136_out, nand_136_out);
  nand nand_147 (nand_147_out, nand_137_out, nand_137_out);
  nand nand_148 (nand_148_out, nand_139_out, nand_139_out);
  nand nand_149 (a, nand_141_out, nand_142_out);
  nand nand_150 (b, nand_143_out, nand_144_out);
  nand nand_151 (d, nand_146_out, nand_147_out);
  nand nand_152 (f, nand_138_out, nand_148_out);
endmodule

module contador9a0 (
  input  Q3,
  input  Q2,
  input  Q1,
  input  Q0,
  output D3,
  output D2,
  output D1,
  output D0
);

  wire and_1_out, and_2_out, and_3_out, and_4_out, and_5_out, and_6_out, and_7_out, and_8_out, not_1_out,
       not_2_out, not_3_out, not_4_out, not_5_out, not_6_out;

  not not_1 (not_1_out, Q1);
  not not_2 (not_2_out, Q0);
  not not_3 (not_3_out, Q3);
  not not_4 (not_4_out, Q2);
  not not_5 (not_5_out, Q1);
  not not_6 (not_6_out, Q0);
  and and_1 (and_1_out, Q3, Q0);
  and and_2 (and_2_out, not_3_out, not_4_out, not_5_out, not_6_out);
  and and_3 (and_3_out, Q0, Q2);
  and and_4 (and_4_out, Q2, Q1);
  and and_5 (and_5_out, Q3, not_2_out);
  and and_6 (and_6_out, Q2, not_1_out, not_2_out);
  and and_7 (and_7_out, not_2_out, Q3);
  and and_8 (and_8_out, Q1, Q0);
  or or_1 (D3, and_1_out, and_2_out);
  or or_2 (D2, and_3_out, and_4_out, and_5_out);
  or or_3 (D1, and_6_out, and_7_out, and_8_out);
  not not_7 (D0, Q0);

  // Notes on the sheet:
  //   CONTADOR DE 9 A 0
endmodule

module contador5a0 (
  input  Q2,
  input  Q1,
  input  Q0,
  output out_4,
  output D1,
  output D0
);

  wire and_1_out, and_2_out, and_3_out, and_4_out, not_1_out, not_2_out, not_3_out;

  not not_1 (not_1_out, Q1);
  not not_2 (not_2_out, Q0);
  not not_3 (not_3_out, Q2);
  and and_1 (and_1_out, Q2, Q0);
  and and_2 (and_2_out, not_3_out, not_1_out, not_2_out);
  and and_3 (and_3_out, Q1, Q0);
  and and_4 (and_4_out, Q2, not_2_out);
  or or_1 (out_4, and_1_out, and_2_out);
  or or_2 (D1, and_3_out, and_4_out);
  not not_4 (D0, Q0);
endmodule

module circuito_display_en (
  input  D3,
  input  D2,
  input  D1,
  input  D0,
  input  EN,
  output a,
  output b,
  output c,
  output d,
  output e,
  output f,
  output g
);

  wire sa, sb, sc, sd, se, sf, sg;

  circuito_display circuito_display_1 (
    .D3(D3), .D2(D2), .D1(D1), .D0(D0), .a(sa), .b(sb), .c(sc), .d(sd), .e(se), .f(sf), .g(sg));
  and and_1 (a, sa, EN);
  and and_2 (b, sb, EN);
  and and_3 (c, sc, EN);
  and and_4 (d, sd, EN);
  and and_5 (e, se, EN);
  and and_6 (f, sf, EN);
  and and_7 (g, sg, EN);

  // Notes on the sheet:
  //   DISPLAY COM ENABLE: segmento = decodificador AND EN
endmodule
